# Fritzing sketch lapa (saved by Fritzing 0.9.3b)
breadboards: 5

parts:
  Part1 = Arduino Nano (Rev3.0) (ICSP)
  U1 = 74HC595 [package="DIP16 [THT]"]
  U4 = 74HC165 [part_number=SN74LS165 package="DIP16 [THT]"]
  U5 = 74HC165 [part_number=SN74LS165 package="DIP16 [THT]"]
  R1 = Resistor [tolerance=±5% resistance=220 package=THT]
  R2 = Resistor [tolerance=±5% resistance=220 package=THT]
  R3 = Resistor [tolerance=±5% resistance=220 package=THT]
  R4 = Resistor [tolerance=±5% resistance=220 package=THT]
  R5 = Resistor [tolerance=±5% resistance=220 package=THT]
  R6 = Resistor [tolerance=±5% resistance=220 package=THT]
  R7 = Resistor [tolerance=±5% resistance=220 package=THT]
  R8 = Resistor [tolerance=±5% resistance=220 package=THT]
  R9 = Resistor [tolerance=±5% resistance=220 package=THT]
  R10 = Resistor [tolerance=±5% resistance=220 package=THT]
  R11 = Resistor [tolerance=±5% resistance=220 package=THT]
  R12 = Resistor [tolerance=±5% resistance=220 package=THT]
  S1 = Pushbutton [package=THT]
  S2 = Pushbutton [package=THT]
  S3 = Pushbutton [package=THT]
  S4 = Pushbutton [package=THT]
  S5 = Pushbutton [package=THT]
  S6 = Pushbutton [package=THT]
  S7 = Pushbutton [package=THT]
  S8 = Pushbutton [package=THT]
  S9 = Pushbutton [package=THT]
  S10 = Pushbutton [package=THT]
  S11 = Pushbutton [package=THT]
  S12 = Pushbutton [package=THT]
  Left = DC Motor
  Right = DC Motor
  Backward = DC Motor
  Forward = DC Motor
  Up = DC Motor
  Down = DC Motor
  8_Channel_Relay1 = 8 Channel Power Relay
  Catch = DC Motor
  J1 = Power Jack [package=power_jack_slot]

nets:
  GND: Part1.GND, U1.GND, U1.OE, U4.GND, U4.Q0, U5.GND, U5.MR, U5.Q0, S1.leg1, S2.leg0, S3.leg0, S4.leg0, S5.leg0, S6.leg0, S7.leg0, S8.leg0, S9.leg0, S10.leg0, S11.leg0, S12.leg0, 8_Channel_Relay1.GND
  N1: Part1.D9, U4.Q1, U5.Q1
  N2: Part1.D10, U1.ST_CP
  N3: Part1.D11/MOSI, U1.DS
  N4: Part1.D12/MISO, U4.Q7'
  5V: Part1.5V, U1.MR, U1.VCC, U4.VCC, U5.VCC, R1.Pin_0, R2.Pin_0, R3.Pin_0, R4.Pin_0, R5.Pin_0, R6.Pin_0, R7.Pin_1, R8.Pin_1, R9.Pin_1, R10.Pin_0, R11.Pin_0, R12.Pin_0, 8_Channel_Relay1.VCC
  N5: Part1.D13/SCK, U1.SH_CP, U4.Q2, U5.Q2
  N6: U1.Q1, 8_Channel_Relay1.IN2
  N7: U1.Q2, 8_Channel_Relay1.IN3
  N8: U1.Q3, 8_Channel_Relay1.IN4
  N9: U1.Q4, 8_Channel_Relay1.IN5
  N10: U1.Q5, 8_Channel_Relay1.IN6
  N11: U1.Q6, 8_Channel_Relay1.IN7
  N12: U1.Q7, 8_Channel_Relay1.IN8
  N13: U1.Q0, 8_Channel_Relay1.IN1
  N14: U4.Q3, R1.Pin_1, S1.leg0
  N15: U4.Q4, R2.Pin_1, S2.leg1
  N16: U4.MR, U5.Q7'
  N17: U4.SH_CP, R9.Pin_0, S3.leg1
  N18: U4.ST_CP, R10.Pin_1, S4.leg1
  N19: U4.OE, R11.Pin_1, S5.leg1
  N20: U4.DS, R12.Pin_1, S6.leg1
  N21: U5.Q3, R7.Pin_0, S7.leg1
  N22: U5.Q4, R8.Pin_0, S8.leg1
  N23: U5.SH_CP, R3.Pin_1, S12.leg1
  N24: U5.ST_CP, R4.Pin_1, S11.leg1
  N25: U5.OE, R6.Pin_1, S10.leg1
  N26: U5.DS, R5.Pin_1, S9.leg1
  N27: Left.pin_1, 8_Channel_Relay1.COM#22
  N28: Left.pin_2, Right.pin_2, Backward.pin_2, Forward.pin_2, Up.pin_2, Down.pin_2, 8_Channel_Relay1.NC, Catch.pin_2, J1.GNDBREAK, J1.GND
  N29: Right.pin_1, 8_Channel_Relay1.COM#25
  N30: Backward.pin_1, 8_Channel_Relay1.COM#28
  N31: Forward.pin_1, 8_Channel_Relay1.COM#31
  N32: Up.pin_1, 8_Channel_Relay1.COM#34
  N33: Down.pin_1, 8_Channel_Relay1.COM#37
  N34: 8_Channel_Relay1.NO#23, 8_Channel_Relay1.NO#26, 8_Channel_Relay1.NO#29, 8_Channel_Relay1.NO#32, 8_Channel_Relay1.NO#35, 8_Channel_Relay1.NO#38, 8_Channel_Relay1.COM#40, J1.PWR
  N35: 8_Channel_Relay1.NO#41, Catch.pin_1

notes:
  Up/Down buttons
  Joystick
  Terminals

custom parts:
  74HC165: 8-bit parallel-load shift registers
  8 Channel Power Relay: An 8 channel power relay. The module operates at 5V.
